# Fritzing sketch sensoria (saved by Fritzing 0.9.4)
circuit board: 8.46667cm x 5.64444cm
breadboards: 1

parts:
  Raspberry_Pi1 = Raspberry Pi 2
  DHT1 = DHT11 Humitidy and Temperature Sensor
  LED1 = LED - 3mm [color="Green (555nm)" package="3 mm [THT]"]
  LED2 = LED - 3mm [color="Red (633nm)" package="3 mm [THT]"]
  LED3 = LED - 3mm [color="Blue (430nm)" package="3 mm [THT]"]
  LED4 = LED - 3mm [color="Green (555nm)" package="3 mm [THT]"]

nets:
  GND: Raspberry_Pi1.GND, DHT1.GND, LED1.cathode, LED2.cathode, LED3.cathode, LED4.cathode
  N1: Raspberry_Pi1.GPIO24, LED3.anode
  N2: Raspberry_Pi1.GPIO23, LED4.anode
  N3: Raspberry_Pi1.GPIO18, LED2.anode
  N4: Raspberry_Pi1.GPIO15, LED1.anode
  N5: Raspberry_Pi1.GPIO14, DHT1.DATA
  5V: Raspberry_Pi1.5V, DHT1.VDD

custom parts:
  DHT11 Humitidy and Temperature Sensor: DHT11 Humidity and Temperature Sensor
